# Fritzing sketch Untitled_Sketch (saved by Fritzing 0.9.3b)

parts:
  Composant1 = Arduino Uno (Rev3)  # not connected
  Composant2 = Arduino Uno (Rev3)
  Arduino_WiFi_Shield1 = Arduino WiFi Shield
  Composant3 = Arduino Ethernet Shield (Rev3)  # not connected
  Composant4 = Arduino Mega 2560 (Rev3)  # not connected
  Composant5 = Arduino Mega 2560 (Rev3)
  Arduino_WiFi_Shield2 = Arduino WiFi Shield
  Composant6 = Arduino Ethernet Shield (Rev3)  # not connected

nets:
  N1: Composant2.A0, Arduino_WiFi_Shield1.A0
  N2: Composant2.A1, Arduino_WiFi_Shield1.A1
  N3: Composant2.A2, Arduino_WiFi_Shield1.A2
  N4: Composant2.A3, Arduino_WiFi_Shield1.A3
  N5: Composant2.A4/SDA, Arduino_WiFi_Shield1.SDA, Arduino_WiFi_Shield1.A4
  N6: Composant2.A5/SCL, Arduino_WiFi_Shield1.SCL, Arduino_WiFi_Shield1.A5
  N7: Composant2.D8, Arduino_WiFi_Shield1.8
  N8: Composant2.D9_PWM, Arduino_WiFi_Shield1.~9
  N9: Composant2.D10_PWM/SS, Arduino_WiFi_Shield1.~10
  N10: Composant2.D11_PWM/MOSI, Arduino_WiFi_Shield1.~11
  N11: Composant2.D12/MISO, Arduino_WiFi_Shield1.12
  N12: Composant2.D13/SCK, Arduino_WiFi_Shield1.13
  GND: Composant2.GND, Arduino_WiFi_Shield1.GND
  N13: Composant2.AREF, Arduino_WiFi_Shield1.AREF
  N14: Composant2.D0/RX, Arduino_WiFi_Shield1.RX_0
  N15: Composant2.D1/TX, Arduino_WiFi_Shield1.TX_1
  N16: Composant2.D2, Arduino_WiFi_Shield1.2
  N17: Composant2.D3_PWM, Arduino_WiFi_Shield1.~3
  N18: Composant2.D4, Arduino_WiFi_Shield1.4
  N19: Composant2.D5_PWM, Arduino_WiFi_Shield1.~5
  N20: Composant2.D6_PWM, Arduino_WiFi_Shield1.~6
  N21: Composant2.D7, Arduino_WiFi_Shield1.7
  N22: Composant2.RESET, Arduino_WiFi_Shield1.RESET
  3V3: Composant2.3V3, Arduino_WiFi_Shield1.3.3V
  5V: Composant2.5V, Arduino_WiFi_Shield1.5V
  VIN: Composant2.VIN, Arduino_WiFi_Shield1.Vin
  N23: Composant5.A0, Arduino_WiFi_Shield2.A0
  N24: Composant5.A1, Arduino_WiFi_Shield2.A1
  N25: Composant5.A2, Arduino_WiFi_Shield2.A2
  N26: Composant5.A3, Arduino_WiFi_Shield2.A3
  N27: Composant5.A4, Arduino_WiFi_Shield2.A4
  N28: Composant5.A5, Arduino_WiFi_Shield2.A5
  N29: Composant5.D21/SCL, Composant5.SCL, Arduino_WiFi_Shield2.SCL
  N30: Composant5.D20/SDA, Composant5.SDA, Arduino_WiFi_Shield2.SDA
  N31: Composant5.AREF, Arduino_WiFi_Shield2.AREF
  GND_2: Composant5.GND, Arduino_WiFi_Shield2.GND
  N32: Composant5.D13_PWM, Arduino_WiFi_Shield2.13
  N33: Composant5.D12_PWM, Arduino_WiFi_Shield2.12
  N34: Composant5.D11_PWM, Arduino_WiFi_Shield2.~11
  N35: Composant5.D10_PWM, Arduino_WiFi_Shield2.~10
  N36: Composant5.D9_PWM, Arduino_WiFi_Shield2.~9
  N37: Composant5.D8_PWM, Arduino_WiFi_Shield2.8
  N38: Composant5.RESET, Arduino_WiFi_Shield2.RESET
  3V3_2: Composant5.3V3, Arduino_WiFi_Shield2.3.3V
  5V_2: Composant5.5V, Arduino_WiFi_Shield2.5V
  VIN_2: Composant5.VIN, Arduino_WiFi_Shield2.Vin
  N39: Composant5.D0_RX0, Arduino_WiFi_Shield2.RX_0
  N40: Composant5.D1_TX0, Arduino_WiFi_Shield2.TX_1
  N41: Composant5.D2_PWM, Arduino_WiFi_Shield2.2
  N42: Composant5.D3_PWM, Arduino_WiFi_Shield2.~3
  N43: Composant5.D4_PWM, Arduino_WiFi_Shield2.4
  N44: Composant5.D5_PWM, Arduino_WiFi_Shield2.~5
  N45: Composant5.D6_PWM, Arduino_WiFi_Shield2.~6
  N46: Composant5.D7_PWM, Arduino_WiFi_Shield2.7

custom parts:
  Arduino WiFi Shield: Arduino WiFi Shield. Requires an Arduino board. Operates at 5V. The shield connects to 802.11b/g networks with WEP and WPA2 Personal encryption.
